# Fritzing sketch besourinoV1.0 (saved by Fritzing 0.9.3b)
circuit board: 7.33cm x 6.75cm
breadboards: 1

parts:
  NANO = Arduino Nano (Rev3.0)
  JP1_POWER = Header 2 [package=molex-1x2_lock]
  M3-servo = Dagu DGServo 9g (Top view) [part_number=RS001B]
  M2-servo = Dagu DGServo 9g (Top view) [part_number=RS001B]
  M1-servo = Dagu DGServo 9g (Top view) [part_number=RS001B]
  R3-10k = Resistor [tolerance=±5% resistance=10k package=THT]
  R4-220 = Resistor [tolerance=±5% resistance=220 package=THT]
  R5-trimpot = TRIMPOT [package=trimpot_pth_s3_lock]
  R6-infrared = Resistor [tolerance=±5% resistance=10k package=THT]
  R7 = Resistor [tolerance=±5% resistance=100 package=THT]
  U1-LM317 = Voltage Regulator - Variable [package="TO220 [THT]"]
  J2-ESP01 = double row female pin header, 8 pins [form="♀ (female)"]
  J4-sonic = female pin header, 4 pins [form="♀ (female)"]
  J5-infra = double row female pin header, 4 pins [form="♀ (female)"]
  R1-2k2 = Resistor [tolerance=±5% resistance=2.2k package=THT]
  R2-3k3 = Resistor [tolerance=±5% resistance=3.3k package=THT]
  buzzer = Buzzer 12mm [package=buzzer-12mm-ns]

nets:
  N1: NANO.D1/TX, R2-3k3.Pin_1
  N2: NANO.D0/RX, J2-ESP01.pin1
  GND: NANO.GND, JP1_POWER.2, M3-servo.gnd, M2-servo.gnd, M1-servo.gnd, R5-trimpot.WIPER, J2-ESP01.pin8, J4-sonic.pin1, J5-infra.pin3, J5-infra.pin4, R1-2k2.Pin_1, buzzer.2
  N3: NANO.D3, buzzer.1
  N4: NANO.D5, M3-servo.pulse
  N5: NANO.D6, M2-servo.pulse
  N6: NANO.D9, M1-servo.pulse
  N7: NANO.D11/MOSI, J4-sonic.pin3
  N8: NANO.D12/MISO, J4-sonic.pin2
  VCC: NANO.VIN, JP1_POWER.1, M3-servo.vcc, M2-servo.vcc, M1-servo.vcc, U1-LM317.IN
  N9: NANO.5V, R6-infrared.Pin_0, R7.Pin_0, J4-sonic.pin4
  N10: NANO.A3, R6-infrared.Pin_1, J5-infra.pin1
  N11: R3-10k.Pin_0, J2-ESP01.pin2
  N12: R3-10k.Pin_1, R4-220.Pin_1, U1-LM317.OUT, J2-ESP01.pin4
  N13: R4-220.Pin_0, R5-trimpot.CCW, U1-LM317.ADJ
  N14: R7.Pin_1, J5-infra.pin2
  N15: J2-ESP01.pin5, R1-2k2.Pin_0, R2-3k3.Pin_0

notes:
  Besourino HW V0.9
